# Fritzing sketch clockyness (saved by Fritzing 1.0.1rc)
breadboards: 1

parts:
  U1 = ESP8266 WiFi Module [part_number=ESP8266]
  R1 = Resistor [tolerance=±5% power=0.25 resistance=150 package=THT]
  R2 = Resistor [tolerance=±5% power=0.25 resistance=200 package=THT]
  RGB_SMD_LED1 = SMD RGB LED (WS2812) [package=5050]
  S1 = SPST Switch [package=switch-spdt_kit]

nets:
  N1: U1.CMD, RGB_SMD_LED1.DOut, S1.P
  N2: U1.D0, R1.Pin_0
  N3: U1.3.3V#10, S1.O
  N4: U1.IO15, RGB_SMD_LED1.VCC
  N5: R1.Pin_1, R2.Pin_0
  N6: R2.Pin_1, RGB_SMD_LED1.DIn

notes:
  this board is jacked... IRL, connect to Vin pin to +5V rail, GND to GND rail LED signal at D5 pin, and Reset switch to D1 pin
